# Fritzing sketch ArduinoPowerOutageDetector_Schematic (saved by Fritzing 0.9.3b)
breadboards: 1

parts:
  Outer_Power_Input = Power plug
  Arduino_MCU = Arduino Nano (Rev3.0)
  Optocoupler = Sharp PC817 [package=THT]
  R1 = Resistor [tolerance=±5% resistance=1k package=THT]
  R2 = Resistor [tolerance=±5% resistance=1k package=THT]
  LED_ON = LED - 5mm [color="Green (570nm)" package="5 mm [THT]"]
  LED_OFF = LED - 5mm [color="Red (633nm)" package="5 mm [THT]"]
  R3 = Resistor [tolerance=±5% resistance=1k package=THT]
  R4 = Resistor [tolerance=±5% resistance=470k package=THT]
  Maintenance_Mode_Switch = Toggle Switch [package=THT]

nets:
  N1: Outer_Power_Input.GND, Optocoupler.Pin_2
  N2: Outer_Power_Input.VCC, R1.Pin_0
  N3: Arduino_MCU.D2, Optocoupler.Pin_3, R4.Pin_0, Maintenance_Mode_Switch.L2
  N4: Arduino_MCU.D3, LED_ON.anode
  N5: Arduino_MCU.D4, LED_OFF.anode
  N6: Arduino_MCU.GND, R3.Pin_1, R4.Pin_1
  N7: Arduino_MCU.5V, R2.Pin_1
  N8: Optocoupler.Pin_1, R1.Pin_1
  N9: Optocoupler.Pin_4, R2.Pin_0, Maintenance_Mode_Switch.COM
  N10: LED_ON.cathode, LED_OFF.cathode, R3.Pin_0
